// Digital circuit LAB SCHEMATIC.dig as structural Verilog
module LAB_SCHEMATIC (
  input  D,
  input  A,
  input  B,
  input  C,
  output Y
);

  wire _7404_1_pin11, _74151_1_pin12, _74151_1_pin13, _74151_1_pin14, _74151_1_pin15;

  _74151 _74151_1 (
    .pin1(D), .pin2(D), .pin3(D), .pin4(D), .pin5(Y), .pin7(1'b0), .pin8(1'b0), .pin9(A), .pin10(B),
    .pin11(C), .pin12(_74151_1_pin12), .pin13(_74151_1_pin13), .pin14(_74151_1_pin14),
    .pin15(_74151_1_pin15), .pin16(1'b1));  // open: pin6
  _7404 _7404_1 (
    .pin1(D), .pin2(_74151_1_pin15), .pin3(D), .pin4(_74151_1_pin14), .pin5(D), .pin6(_74151_1_pin13),
    .pin7(1'b0), .pin8(_74151_1_pin12), .pin9(D), .pin11(_7404_1_pin11), .pin13(_7404_1_pin11), .pin14(1'b1));  // open: pin10, pin12
  // NotConnected on _7404_1_pin11
endmodule

/* Test case:
D C B A Y
0 0 0 0 0
0 0 0 1 1
0 0 1 0 0
0 0 1 1 1
0 1 0 0 0
0 1 0 1 1
0 1 1 0 0
0 1 1 1 1
1 0 0 0 1
1 0 0 1 0
1 0 1 0 1
1 0 1 1 0
1 1 0 0 1
1 1 0 1 x
1 1 1 0 x
1 1 1 1 x
*/
